# Fritzing sketch IRArray (saved by Fritzing 0.9.1b)

parts:
  Part1 = Arduino Uno (Rev3)
  QTR-8A_IR_emitter/reciever_line_sensing_array1 = Pololu QTR-8A IR Sensor Array

nets:
  N1: Part1.A0, QTR-8A_IR_emitter/reciever_line_sensing_array1.PIN_1
  N2: Part1.A1, QTR-8A_IR_emitter/reciever_line_sensing_array1.PIN_2
  N3: Part1.A2, QTR-8A_IR_emitter/reciever_line_sensing_array1.PIN_3
  N4: Part1.A3, QTR-8A_IR_emitter/reciever_line_sensing_array1.PIN_4
  N5: Part1.A4/SDA, QTR-8A_IR_emitter/reciever_line_sensing_array1.PIN_5
  N6: Part1.A5/SCL, QTR-8A_IR_emitter/reciever_line_sensing_array1.PIN_6
